# Fritzing sketch Sketch (saved by Fritzing 0.8.7b)

parts:
  Part1 = Arduino Uno (Rev3)
  U1 = LM2596 step down module
  U2 = LM2596 step down module
  SIM800L_BO1 = SIM800L BO
  Part2 = SRF05 Ultrasonic Rangefinder
  JP1 = Header 2 [package=screwterminal-3.5mm-2_lock]
  Display1 = LCD screen 16x2 IIC [part_number=101290]
  Part3 = Tiny RTC - DS1307 Breakout Board
  J1 = Basic Servo
  R1 = Photocell (LDR) [package=THT]
  KY-1 = Keyes Relay [package=THT]
  KY-2 = Keyes Relay [package=THT]
  J2 = Piezo Speaker
  S1 = PH meter [package=THT]

nets:
  N1: Part1.A0, R1.pin_0
  N2: Part1.A1, S1.pin1
  N3: Part1.A4/SDA, Display1.SDA, Part3.SDA
  N4: Part1.A5/SCL, Display1.SCL, Part3.SCL
  N5: Part1.D8, J1.pulse
  GND: Part1.GND, U1.IN-, U1.OUT-, U2.IN-, U2.OUT-, SIM800L_BO1.pin_6, Part2.GND, JP1.1, Display1.GND, Part3.GND, J1.gnd, R1.pin_1
  N6: Part1.D0/RX, SIM800L_BO1.pin_5
  N7: Part1.D1/TX, SIM800L_BO1.pin_4
  N8: Part1.D2, SIM800L_BO1.PIN3
  N9: Part1.D3_PWM, KY-1.signal
  N10: Part1.D4, KY-2.signal
  N11: Part1.D5_PWM, J2.pin1
  N12: Part1.D6_PWM, Part2.Trig
  N13: Part1.D7, Part2.Echo
  VCC: Part1.5V, U2.OUT+, Part2.VCC, Display1.VCC, Part3.VCC, J1.vcc, KY-1.power, KY-2.power
  N14: U1.IN+, U2.IN+, JP1.2
  N15: U1.OUT+, SIM800L_BO1.PIN2
  N16: KY-1.ground, KY-2.ground, S1.pin3
  N17: J2.pin2, S1.pin2

custom parts:
  LM2596 step down module: LM2596 DC-DC step down power supply module 3 A.
  LCD screen 16x2 IIC: LCD screen with HD44780 controller enables showing text, symbols, value or anything else that comes from Croduino/Arduino. It is capable of showing 16 symbols in two lines and therefore can be used in many projects that need to send clearly visible and legible output information.. • Color of symbols: White • Backlight: Blue • Dimensions: 80 x 36 x 12 mm • Screen dimensions: 64.5 x 16 mm •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
  Tiny RTC - DS1307 Breakout Board: The Tiny RTC is a breakout board for the Dallas Semiconductor/Maxim Integrated DS1307 real-time clock. The DS1307 counts seconds, minutes, hours, date of the month, month, day of the week, and year (with compensation for leap-years). The breakout board also has space for a DS18B20 digital thermometer.
  Keyes Relay: The Keyes 5V relay module is suitable for SCM development, home appliance control. It uses a 5V~12V TIL control signal which can control DC / AC signal.
